# Fritzing sketch lefton (saved by Fritzing 0.9.3b)
breadboards: 1

parts:
  Part1 = Arduino Pro Mini (5V)
  M1 = DC Motor  # not connected
  S2 = Pushbutton [package="[THT]"]
  S4 = SWITCH-SP3T [package=switch-sp3t-smd]
  S5 = Pushbutton [package="[THT]"]
  VCC1 = Battery
  S6 = Pushbutton [package="[THT]"]
  S7 = Pushbutton [package="[THT]"]
  S8 = Pushbutton [package="[THT]"]
  S9 = Pushbutton [package="[THT]"]

nets:
  N1: Part1.RXI, VCC1.+
  N2: Part1.GND, S4.3, S5.Pin_4, VCC1.-, S6.Pin_4, S7.Pin_4, S8.Pin_3, S8.Pin_4, S9.Pin_3, S9.Pin_4
  N3: Part1.A1, S9.Pin_1, S9.Pin_2
  N4: Part1.A0, S8.Pin_1, S8.Pin_2
  N5: Part1.D9, S4.4
  N6: Part1.D8, S4.2
  N7: Part1.D7, S4.1
  N8: Part1.D6, S2.Pin_1
  N9: Part1.D5, S5.Pin_1, S5.Pin_2
  N10: Part1.D4, S6.Pin_1, S6.Pin_2
  N11: Part1.D3, S7.Pin_1, S7.Pin_2
